# Fritzing sketch LedLamp (saved by Fritzing 0.9.3b)

parts:
  Часть1 = Arduino Pro Mini v13
  S1 = Pushbutton [part_number=BUTTON package="[THT]"]
  J1 = female pin header, 2 pins [form="♀ (female)" part_number="LED STRIP LIGHTS"]
  J2 = female pin header, 2 pins [form="♀ (female)" part_number=+12V]
  R1 = Resistor [tolerance=±5% resistance=10k package=THT]
  R2 = Resistor [tolerance=±5% resistance=10k package=THT]
  Q1 = MOSFET-NCHANNEL [part_number=IRF630 package=sot323]
  U1 = DC-DC_CONVERTER [package=dc-dc_converter]

nets:
  N1: Часть1.VCC, R1.Pin_1, R2.Pin_0, U1.VOUT
  N2: Часть1.D5_PWM, S1.Pin_1, S1.Pin_2, R1.Pin_0
  N3: Часть1.D3_PWM, R2.Pin_1, Q1.G
  GND: Часть1.GND, S1.Pin_3, S1.Pin_4, J2.pin1, Q1.S, U1.GND1, U1.GND2
  N4: J1.pin1, J2.pin2, U1.VIN
  N5: J1.pin2, Q1.D

// code stored in the sketch: LedLamp.ino
const int pinButton = 5;
const int pinLed = 3;  // external led strip lights

int pinLedState = LOW;
int pinButtonState;
int lastButtonState = HIGH;

unsigned long lastDebounceTime = 0;  // the last time the output pin was toggled
unsigned long debounceDelay = 50;    // the debounce time; increase if the output flickers

bool isButtonPressed = false; 
unsigned long holdDelay = 2000;
unsigned long holdLastTime = 0; 

bool timerIsActivated = false;
unsigned long timerDelay = 30 * 60000; // power off time
unsigned long timerTime = 0;

void setup() {

  pinMode(pinButton, INPUT);
  pinMode(pinLed, OUTPUT);
  pinMode(LED_BUILTIN, OUTPUT);

  digitalWrite(pinLed, pinLedState);
  digitalWrite(LED_BUILTIN, pinLedState);  

  Serial.begin(9600);
  Serial.println("Initialization done");
}

void ledSignal() {

  Serial.println("Timer activated");
  timerIsActivated = true;
  timerTime = millis();

  digitalWrite(pinLed, HIGH);
  delay(1000);
  digitalWrite(pinLed, LOW);
  delay(400);
  digitalWrite(pinLed, HIGH);
  delay(1000);
  digitalWrite(pinLed, LOW);
  delay(400);
  digitalWrite(pinLed, HIGH);
  delay(1000);
  digitalWrite(pinLed, LOW);
  delay(400);
  digitalWrite(pinLed, HIGH);
  pinLedState = HIGH;
  
}

void btnLoop() {
//  Serial.println("btnLoop");

  if (!isButtonPressed) { 
    isButtonPressed = true;
    holdLastTime = millis();
    Serial.println("btnLoop activated");
  }

  if (isButtonPressed) {
    if (millis() - holdLastTime > holdDelay) {
      holdLastTime = 0;
      isButtonPressed = false;
      ledSignal();
    }
  }
  
}

void timerCheck() {

  Serial.println("Timer check");

  if (millis() - timerTime > timerDelay) {
    Serial.println("Timer completed");
    timerTime = 0;
    timerIsActivated = false;
    pinLedState = LOW;
  }
}

void loop() {
  
  int reading = digitalRead(pinButton);

  if (reading != lastButtonState) {
    lastDebounceTime = millis();
  }

  if ((millis() - lastDebounceTime) > debounceDelay) {

    if ((pinButtonState == LOW) and isButtonPressed) {
      btnLoop();
    }

    if (reading != pinButtonState) {
      pinButtonState = reading;     

      if (pinButtonState == LOW) {
        Serial.println("Button pressed");
        btnLoop();
      } else {
        if (isButtonPressed) {
          holdLastTime = 0;
          isButtonPressed = false;
          pinLedState = !pinLedState;
          Serial.print("Led state: ");
          Serial.println(pinLedState);
        } 
      }
    
    }
 
  }

  lastButtonState = reading;
//===========================================================

  if (timerIsActivated) timerCheck();
  digitalWrite(pinLed, pinLedState);

}
